# Fritzing sketch GPSTESTING (saved by Fritzing 0.9.2b)
breadboards: 1

parts:
  Part1 = Arduino Nano (Rev3.0)
  LCD2004-I2C1 = LCD2004-I2C
  U1 = SUP500F [package=sup500f]

nets:
  GND: Part1.GND, LCD2004-I2C1.GND, U1.GND
  N1: Part1.D3, U1.RX-I
  N2: Part1.D4, U1.TX-O
  VIN: Part1.VIN, LCD2004-I2C1.VCC
  5V: Part1.5V, U1.VCC
  N3: Part1.A5, LCD2004-I2C1.SCL
  N4: Part1.A4, LCD2004-I2C1.SDA

custom parts:
  LCD2004-I2C: A standard character display with 4x20 characters. Comes in many colors with LCM2004 IIC attached.
